// Logisim project BASIC_PC.circ as structural Verilog
module main (
  input  in_1,
  input  in_2,
  input  in_3,
  input  in_4,
  input  in_5,
  input  in_6,
  output [11:0] out_7,
  output [11:0] out_8,
  output [15:0] out_9,
  output [15:0] out_10,
  output [15:0] out_11,
  output [15:0] out_12
);

  wire AC_ADD, AC_AND, AC_LOAD, and_1_out, and_2_out, and_4_out, and_5_out, and_6_out, and_7_out, and_13_out,
       and_14_out, and_15_out, and_17_out, and_18_out, and_19_out, and_20_out, AR_LOAD, CLK, DR_INC, DR_LOAD,
       IR_LOAD, MEM_READ, MEM_WRITE, OP_ADD, OP_AND, OP_BUN, OP_ISZ, OP_LDA, OP_STA, or_1_out, or_2_out,
       or_3_out, or_8_out, PC_INC, PC_ISZ, PC_LOAD, PC_SRC, SC_CLR, T0, T2, T3, T4, T5, T6, TR_LOAD;
  wire [2:0] BUS_SEL;
  wire [3:0] counter_1_q;
  wire [11:0] adder_1_out, BUS_IN, multiplexer_1_out;
  wire [15:0] AC_IN, ADD_OUT, AND_OUT, BUS, CMA_OUT, DR_IN, INC_OUT, MEM_OUT;

  and and_1 (and_1_out, PC_LOAD, CLK);
  Register #(.width(12)) PC (.D(multiplexer_1_out), .en(and_1_out), .Q(out_7), .clk(CLK), .clr(in_1));
  Adder #(.width(12)) adder_1 (.a(out_7), .b(12'h1), .out(adder_1_out), .cin(1'b0));  // open: cout
  RAM #(.addrWidth(12), .dataWidth(16)) ram_1 (
    .addr(out_8), .data(MEM_OUT), .sel(1'b1), .clk(CLK), .ld(1'b1));  // open: clr
  Multiplexer #(.width(12)) multiplexer_1 (
    .in0(adder_1_out), .in1(BUS_IN), .out(multiplexer_1_out), .sel(PC_SRC));  // open: en
  and and_2 (and_2_out, AR_LOAD, CLK);
  Register #(.width(12)) AR (.D(BUS_IN), .en(and_2_out), .Q(out_8), .clk(CLK), .clr(in_2));
  Adder #(.width(16)) adder_2 (.a(AC_IN), .b(DR_IN), .out(ADD_OUT));  // open: cin, cout
  assign AND_OUT = AC_IN & DR_IN;  // AND_Gate and_3, 16 bits wide
  assign CMA_OUT = ~AC_IN;  // NOT_Gate not_1, 16 bits wide
  Adder #(.width(16)) adder_3 (.a(AC_IN), .b(16'h1), .out(INC_OUT));  // open: cin, cout
  Clock clock_1 (.out(CLK));
  and and_4 (and_4_out, DR_LOAD, CLK);
  Register #(.width(16)) DR (.D(BUS), .en(and_4_out), .Q(out_9), .clk(CLK), .clr(in_3));
  Counter #(.width(4), .max('hf)) counter_1 (.Q(counter_1_q), .clk(CLK), .clr(SC_CLR));  // open: load, D, count, carry
  Decoder #(.select(3)) decoder_1 (
    .out0(OP_AND), .out1(OP_ADD), .out2(OP_LDA), .out3(OP_STA), .out4(OP_BUN), .out5(OP_ISZ),
    .sel(out_11[14:12]));  // open: out6, out7, en
  Decoder #(.select(4)) decoder_2 (
    .out0(T0), .out1(IR_LOAD), .out2(T2), .out3(T3), .out4(T4), .out5(T5), .out6(T6), .sel(counter_1_q));  // open: out7, out8, out9, out10, out11, out12, out13, out14, out15, en
  or or_1 (or_1_out, OP_AND, OP_ADD, OP_LDA);
  or or_2 (or_2_out, OP_AND, OP_ADD, OP_LDA, OP_ISZ);
  and and_5 (and_5_out, OP_STA, T4);
  and and_6 (and_6_out, OP_ISZ, T5);
  or or_3 (or_3_out, OP_AND, OP_ADD, OP_LDA, OP_STA, OP_BUN, OP_ISZ);
  and and_7 (and_7_out, or_1_out, T4);
  and and_8 (DR_LOAD, or_2_out, T5);
  and and_9 (AC_AND, OP_AND, T5);
  and and_10 (AC_ADD, OP_AND, T5);
  and and_11 (AC_LOAD, OP_LDA, T5);
  and and_12 (DR_INC, OP_ISZ, T5);
  and and_13 (and_13_out, PC_ISZ, T6);
  and and_14 (and_14_out, AC_LOAD, CLK);
  and and_15 (and_15_out, or_3_out, T3);
  or or_4 (MEM_READ, and_7_out, IR_LOAD);
  or or_5 (MEM_WRITE, and_5_out, and_6_out);
  and and_16 (PC_LOAD, OP_BUN, T4);
  Register #(.width(16)) AC (.D(BUS), .en(and_14_out), .Q(out_10), .clk(CLK), .clr(in_4));
  or or_6 (AR_LOAD, and_15_out, T0);
  or or_7 (PC_INC, and_13_out, IR_LOAD);
  or or_8 (or_8_out, OP_AND, OP_ADD, OP_LDA, OP_STA, OP_BUN);
  and and_17 (and_17_out, or_8_out, T4);
  and and_18 (and_18_out, OP_ISZ, T6);
  or or_9 (SC_CLR, and_17_out, and_18_out);
  and and_19 (and_19_out, IR_LOAD, CLK);
  Register #(.width(16)) IR (.D(BUS), .en(and_19_out), .Q(out_11), .clk(CLK), .clr(in_5));
  and and_20 (and_20_out, TR_LOAD, CLK);
  Multiplexer #(.select(3), .width(16)) multiplexer_2 (
    .in0({out_8, 4'b0000}), .in1({out_7, 4'b0000}), .in2(out_9), .in3(out_10), .in4(out_11), .in5(out_12),
    .in6(MEM_OUT), .out(BUS), .sel(BUS_SEL));  // open: in7, en
  Register #(.width(16)) TR (.D(BUS), .en(and_20_out), .Q(out_12), .clk(CLK), .clr(in_6));

  // Other names for the same wires on the sheet: AR_OUT[11:0] = out_8; PC_OUT[11:0] = out_7; AC_OUT[15:0] = out_10;
  //   DR_OUT[15:0] = out_9; ADDR_FIELD[11:0] = out_11[11:0]; IR_OUT[15:0] = out_11; OPCODE[2:0] = out_11[14:12];
  //   I_BIT = out_11[15]; T1 = IR_LOAD; TR_OUT[15:0] = out_12
endmodule

// PC
module Register_PC (
  input  in_1,
  output [11:0] out_2
);

  wire and_1_out, CLK, PC_LOAD, PC_SRC;
  wire [11:0] adder_1_out, BUS_IN, multiplexer_1_out;

  and and_1 (and_1_out, PC_LOAD, CLK);
  Register #(.width(12)) PC (.D(multiplexer_1_out), .en(and_1_out), .Q(out_2), .clk(CLK), .clr(in_1));
  Adder #(.width(12)) adder_1 (.a(out_2), .b(12'h1), .out(adder_1_out));  // open: cin, cout
  Multiplexer #(.width(12)) multiplexer_1 (
    .in0(adder_1_out), .in1(BUS_IN), .out(multiplexer_1_out), .sel(PC_SRC));  // open: en

  // Other names for the same wires on the sheet: PC_OUT[11:0] = out_2
endmodule

// AR
module Register_AR (
  output [11:0] out_1
);

  wire and_1_out, AR_LOAD, CLK;
  wire [11:0] BUS_IN;

  and and_1 (and_1_out, AR_LOAD, CLK);
  Register #(.width(12)) AR (.D(BUS_IN), .en(and_1_out), .Q(out_1), .clk(CLK));  // open: clr

  // Other names for the same wires on the sheet: AR_OUT[11:0] = out_1
endmodule

// DR
module Register_DR (
  output [15:0] out_1
);

  wire and_1_out, CLK, DR_LOAD;
  wire [15:0] BUS_IN;

  and and_1 (and_1_out, DR_LOAD, CLK);
  Register #(.width(16)) DR (.D(BUS_IN), .en(and_1_out), .Q(out_1), .clk(CLK));  // open: clr

  // Other names for the same wires on the sheet: DR_OUT[15:0] = out_1
endmodule

// AC
module Register_AC (
  output [15:0] out_1
);

  wire AC_LOAD, AC_SRC, and_1_out, CLK;
  wire [15:0] ALU_RESULT, BUS_IN, multiplexer_1_out;

  Multiplexer #(.width(16)) multiplexer_1 (
    .in0(BUS_IN), .in1(ALU_RESULT), .out(multiplexer_1_out), .sel(AC_SRC));  // open: en
  and and_1 (and_1_out, AC_LOAD, CLK);
  Register #(.width(16)) AC (.D(multiplexer_1_out), .en(and_1_out), .Q(out_1), .clk(CLK));  // open: clr

  // Other names for the same wires on the sheet: AC_OUT[15:0] = out_1
endmodule

// IR
module Register_IR (
  output [15:0] out_1
);

  wire and_1_out, CLK, IR_LOAD;
  wire [15:0] BUS_IN;

  and and_1 (and_1_out, IR_LOAD, CLK);
  Register #(.width(16)) IR (.D(BUS_IN), .en(and_1_out), .Q(out_1), .clk(CLK));  // open: clr

  // Other names for the same wires on the sheet: IR_OUT[15:0] = out_1
endmodule

// TR
module Register_TR (
  output [15:0] out_1
);

  wire and_1_out, CLK, TR_LOAD, undriven;
  wire [15:0] BUS_IN;

  and and_1 (and_1_out, TR_LOAD, CLK);
  Register #(.width(16)) TR (.D(BUS_IN), .en(and_1_out), .Q(out_1), .clk(CLK), .clr(undriven));

  // Other names for the same wires on the sheet: TR_OUT[15:0] = out_1
endmodule

// C_BUS
module CommonBus (
);

  wire [2:0] BUS_SEL;
  wire [11:0] AR_OUT, PC_OUT;
  wire [15:0] AC_OUT, BUS, DR_OUT, IR_OUT, MEM_OUT, TR_OUT;

  Multiplexer #(.select(3), .width(16)) multiplexer_1 (
    .in0({AR_OUT, 4'b0000}), .in1({PC_OUT, 4'b0000}), .in2(DR_OUT), .in3(AC_OUT), .in4(IR_OUT), .in5(TR_OUT),
    .in6(MEM_OUT), .out(BUS), .sel(BUS_SEL));  // open: in7, en
endmodule

// MU
module Memory_Unit (
);

  wire CLK, MEM_READ, undriven;
  wire [11:0] AR_OUT;
  wire [15:0] AC_OUT;

  RAM #(.addrWidth(12), .dataWidth(16)) ram_1 (
    .addr(AR_OUT), .data(AC_OUT), .sel(undriven), .clk(CLK), .ld(MEM_READ));  // open: clr

  // Other names for the same wires on the sheet: MEM_OUT[15:0] = AC_OUT
endmodule

// ALUNIT
module ALU (
);

  wire [15:0] AC_IN, ADD_OUT, AND_OUT, CMA_OUT, DR_IN, INC_OUT;

  Adder #(.width(16)) adder_1 (.a(AC_IN), .b(DR_IN), .out(ADD_OUT));  // open: cin, cout
  assign CMA_OUT = ~AC_IN;  // NOT_Gate not_1, 16 bits wide
  Adder #(.width(16)) adder_2 (.a(AC_IN), .b(16'h1), .out(INC_OUT));  // open: cin, cout
  assign AND_OUT = AC_IN & DR_IN;  // AND_Gate and_1, 16 bits wide
endmodule

// CU
module ControlUnit (
);

  wire AC_ADD, AC_AND, AC_LOAD, and_1_out, and_3_out, and_4_out, and_10_out, and_11_out, and_12_out,
       and_13_out, AR_LOAD, CLK, DR_INC, DR_LOAD, IR_LOAD, MEM_READ, MEM_WRITE, OP_ADD, OP_AND, OP_BUN,
       OP_ISZ, OP_LDA, OP_STA, or_1_out, or_2_out, or_3_out, or_8_out, PC_INC, PC_ISZ, PC_LOAD, SC_CLR, T0,
       T2, T3, T4, T5, T6;
  wire [3:0] counter_1_q;
  wire [14:12] IR_OUT;

  Counter #(.width(4), .max('hf)) counter_1 (.Q(counter_1_q), .clk(CLK), .clr(SC_CLR));  // open: load, D, count, carry
  Decoder #(.select(3)) decoder_1 (
    .out0(OP_AND), .out1(OP_ADD), .out2(OP_LDA), .out3(OP_STA), .out4(OP_BUN), .out5(OP_ISZ), .sel(IR_OUT));  // open: out6, out7, en
  Decoder #(.select(4)) decoder_2 (
    .out0(T0), .out1(IR_LOAD), .out2(T2), .out3(T3), .out4(T4), .out5(T5), .out6(T6), .sel(counter_1_q));  // open: out7, out8, out9, out10, out11, out12, out13, out14, out15, en
  or or_1 (or_1_out, OP_AND, OP_ADD, OP_LDA);
  or or_2 (or_2_out, OP_AND, OP_ADD, OP_LDA, OP_ISZ);
  or or_3 (or_3_out, OP_AND, OP_ADD, OP_LDA, OP_STA, OP_BUN, OP_ISZ);
  and and_1 (and_1_out, or_1_out, T4);
  and and_2 (DR_LOAD, or_2_out, T5);
  and and_3 (and_3_out, OP_STA, T4);
  and and_4 (and_4_out, OP_ISZ, T5);
  or or_4 (MEM_READ, and_1_out, IR_LOAD);
  and and_5 (AC_AND, OP_AND, T5);
  and and_6 (AC_ADD, OP_AND, T5);
  and and_7 (AC_LOAD, OP_LDA, T5);
  or or_5 (MEM_WRITE, and_3_out, and_4_out);
  and and_8 (PC_LOAD, OP_BUN, T4);
  and and_9 (DR_INC, OP_ISZ, T5);
  and and_10 (and_10_out, PC_ISZ, T6);
  and and_11 (and_11_out, or_3_out, T3);
  or or_6 (PC_INC, and_10_out, IR_LOAD);
  or or_7 (AR_LOAD, and_11_out, T0);
  or or_8 (or_8_out, OP_AND, OP_ADD, OP_LDA, OP_STA, OP_BUN);
  and and_12 (and_12_out, or_8_out, T4);
  and and_13 (and_13_out, OP_ISZ, T6);
  or or_9 (SC_CLR, and_12_out, and_13_out);

  // Other names for the same wires on the sheet: OPCODE[2:0] = IR_OUT; T1 = IR_LOAD
endmodule

module TopLevel (
  output [11:0] out_1,
  output [11:0] out_2,
  output [15:0] out_3,
  output [15:0] out_4,
  output [15:0] out_5,
  output [15:0] out_6
);

  wire CLK;

  Register_PC register_pc_1 (.in_1(CLK), .out_2(out_1));
  Register_AR register_ar_1 (.out_1(out_2));
  Register_DR register_dr_1 (.out_1(out_3));
  Register_AC register_ac_1 (.out_1(out_4));
  Register_IR register_ir_1 (.out_1(out_5));
  Register_TR register_tr_1 (.out_1(out_6));
  CommonBus commonbus_1 ();
  Clock clock_1 (.out(CLK));
  Memory_Unit memory_unit_1 ();
  ALU alu_1 ();
  ControlUnit controlunit_1 ();

  // Other names for the same wires on the sheet: AC_OUT[15:0] = out_4; AR_OUT[11:0] = out_2; DR_OUT[15:0] = out_3;
  //   IR_OUT[15:0] = out_5; PC_OUT[11:0] = out_1; TR_OUT[15:0] = out_6
endmodule
