// Logisim project CPU.circ as structural Verilog: 13 circuits, main circuit main
module CPU_TOP (
  output [15:0] out_1,
  output out_2,
  output out_3,
  output out_4,
  output out_5,
  output out_6,
  output out_7,
  output [11:0] out_8,
  output out_9,
  output out_10,
  output out_11,
  output out_12,
  output out_13,
  output out_14,
  output out_15,
  output out_16,
  output out_17,
  output [11:0] out_18,
  output out_19,
  output out_20,
  output out_21,
  output out_22,
  output out_23,
  output out_24,
  output [15:0] out_25,
  output out_26,
  output out_27,
  output [15:0] out_28,
  output [15:0] out_29
);

  wire a0, a1, a2, and_1_out, and_2_out, and_3_out, and_4_out, and_5_out, and_6_out, and_7_out, and_8_out,
       and_9_out, and_10_out, and_11_out, and_12_out, and_13_out, and_14_out, and_16_out, and_17_out,
       and_18_out, and_19_out, and_20_out, and_21_out, and_22_out, and_23_out, and_24_out, and_25_out,
       and_26_out, and_27_out, and_28_out, and_29_out, and_30_out, and_31_out, and_32_out, and_33_out, CLK,
       not_1_out, not_2_out, not_3_out, not_4_out, not_5_out, not_6_out, not_8_out, not_9_out, not_10_out,
       not_11_out, not_12_out, not_13_out, not_14_out, not_15_out, or_1_out, or_2_out, or_4_out, or_5_out,
       or_6_out, or_7_out, or_8_out, or_9_out, or_10_out, or_11_out, or_12_out, or_13_out, or_14_out,
       or_15_out, or_16_out, or_17_out, or_21_out, or_22_out, or_23_out, or_27_out, PC_INC, s0, s1, s2,
       SC_CLR;
  wire [2:0] counter_1_q;
  wire [11:0] adder_1_out, multiplexer_1_out;
  wire [15:0] ALU_OUT, BUS_OUT, CIL, CIR, CMA_AC, INC_AC, M_ADD, M_AND;

  and and_1 (and_1_out, out_7, out_28[15]);
  and and_2 (and_2_out, out_28[15], out_11);
  or or_1 (or_1_out, and_1_out, and_2_out);
  not not_1 (not_1_out, out_26);
  not not_2 (not_2_out, out_26);
  Adder #(.width(12)) adder_1 (.a(out_18), .b(12'h1), .out(adder_1_out));  // open: cin, cout
  and and_3 (and_3_out, out_12, or_1_out, out_26, not_3_out);
  not not_3 (not_3_out, out_29[15]);
  and and_4 (and_4_out, not_1_out, out_29[15], out_12);
  and and_5 (and_5_out, out_15, or_2_out);
  or or_2 (or_2_out, out_3, out_6, out_10);
  and and_6 (and_6_out, out_12, not_2_out, out_29[15]);
  or or_3 (PC_INC, out_5, and_3_out);
  or or_4 (or_4_out, out_3, out_6, out_10);
  and and_7 (and_7_out, out_12, not_4_out, or_5_out, out_26);
  not not_4 (not_4_out, out_29[15]);
  or or_5 (or_5_out, out_24, out_14);
  or or_6 (or_6_out, out_3, out_6, out_10);
  and and_8 (and_8_out, or_6_out, out_19);
  or or_7 (or_7_out, out_5, and_4_out, and_5_out);
  or or_8 (or_8_out, out_2, out_9, and_6_out);
  Multiplexer #(.width(12)) multiplexer_1 (
    .in0(BUS_OUT[11:0]), .in1(adder_1_out), .out(multiplexer_1_out), .sel(PC_INC));  // open: en
  and and_9 (and_9_out, out_15, or_4_out);
  or or_9 (or_9_out, and_7_out, and_8_out);
  Register #(.width(12)) ADDRESS_REGISTER (.D(BUS_OUT[11:0]), .en(or_8_out), .Q(out_8), .clk(CLK));  // open: clr
  and and_10 (and_10_out, out_7, out_28[15]);
  and and_11 (and_11_out, out_28[15], out_11);
  Register #(.width(16)) DATA_REGISTER (.D(BUS_OUT), .en(and_9_out), .Q(out_25), .clk(CLK));  // open: clr
  Register #(.width(16)) ACCUMULATOR (.D(ALU_OUT), .en(or_9_out), .Q(out_28), .clk(CLK), .clr(and_12_out));
  and and_12 (and_12_out, not_6_out, out_26, out_27, out_12);
  Register #(.width(16)) INSTRUCTION_REGISTER (
    .D(BUS_OUT), .en(out_5),
    .Q({out_29[15:12], out_27, out_29[10], out_24, out_29[8], out_21, out_17, out_14, out_11, out_7, out_4, out_29[1:0]}),
    .clk(CLK));  // open: clr
  RAM #(.addrWidth(12), .dataWidth(16)) ram_1 (
    .addr(out_8), .data(out_1), .sel(or_7_out), .clk(CLK), .ld(or_7_out));  // open: clr
  or or_10 (or_10_out, and_10_out, and_11_out);
  not not_5 (not_5_out, out_29[15]);
  not not_6 (not_6_out, out_29[15]);
  and and_13 (and_13_out, out_12, or_10_out, out_26, not_5_out);
  Register #(.width(12)) PROGRAM_COUNTER (.D(multiplexer_1_out), .en(or_11_out), .Q(out_18), .clk(CLK));  // open: clr
  or or_11 (or_11_out, out_5, and_13_out, and_14_out);
  and and_14 (and_14_out, out_15, out_16);
  assign CMA_AC = ~out_28;  // NOT_Gate not_7, 16 bits wide
  Adder #(.width(16)) adder_2 (.a(out_28), .b(out_25), .out(M_ADD));  // open: cin, cout
  Shifter #(.width(16), .shift("rr")) shifter_1 (.in(out_28), .\dist (4'b0001), .out(CIR));
  Shifter #(.width(16), .shift("rl")) shifter_2 (.in(out_28), .\dist (4'b0001), .out(CIL));
  not not_8 (not_8_out, out_26);
  not not_9 (not_9_out, out_26);
  Adder #(.width(16)) adder_3 (.a(out_28), .b(16'h1), .out(INC_AC));  // open: cin, cout
  assign M_AND = out_28;  // AND_Gate and_15, 16 bits wide AND_Gate
  and and_16 (and_16_out, not_8_out, out_12, out_29[15]);
  or or_12 (or_12_out, out_3, out_6, out_10);
  and and_17 (and_17_out, not_9_out, out_12, out_29[15]);
  or or_13 (or_13_out, out_3, out_6, out_10);
  not not_10 (not_10_out, out_26);
  and and_18 (and_18_out, not_10_out, out_12, out_29[15]);
  or or_14 (or_14_out, out_3, out_6, out_10);
  and and_19 (and_19_out, out_15, or_12_out);
  and and_20 (and_20_out, out_15, or_13_out);
  and and_21 (and_21_out, out_15, or_14_out);
  Multiplexer #(.select(3), .width(16)) multiplexer_2 (
    .in1({4'b0000, out_8}), .in2({4'b0000, out_18}),
    .in5({out_29[15:12], out_27, out_29[10], out_24, out_29[8], out_21, out_17, out_14, out_11, out_7, out_4, out_29[1:0]}),
    .in7(out_1), .out(BUS_OUT), .sel({s2, s1, s0}));  // open: in0, in3, in4, in6, en
  or or_15 (or_15_out, out_5, and_16_out, and_19_out);
  or or_16 (or_16_out, out_5, and_17_out, and_20_out);
  or or_17 (or_17_out, out_5, and_18_out, and_21_out);
  and and_22 (and_22_out, out_16, out_15);
  or or_18 (s2, or_15_out, out_9);
  or or_19 (s1, or_16_out, out_2);
  or or_20 (s0, or_17_out, out_9, and_22_out);
  not not_11 (not_11_out, out_29[15]);
  not not_12 (not_12_out, out_29[15]);
  not not_13 (not_13_out, out_29[15]);
  or or_21 (or_21_out, out_14, out_21, out_17);
  and and_23 (and_23_out, out_6, out_19);
  not not_14 (not_14_out, out_29[15]);
  or or_22 (or_22_out, out_24, out_17);
  or or_23 (or_23_out, out_6, out_10);
  Multiplexer #(.select(3), .width(16)) multiplexer_3 (
    .in1(CMA_AC), .in2(INC_AC), .in3(M_ADD), .in4(M_AND), .in5(out_25), .in6(CIR), .in7(CIL), .out(ALU_OUT),
    .sel({a2, a1, a0}));  // open: in0, en
  and and_24 (and_24_out, out_3, out_19);
  and and_25 (and_25_out, out_12, not_11_out, out_21, out_26);
  and and_26 (and_26_out, out_12, not_12_out, out_17, out_26);
  and and_27 (and_27_out, out_10, out_19);
  and and_28 (and_28_out, out_12, not_13_out, out_26, or_21_out);
  and and_29 (and_29_out, out_12, not_14_out, or_22_out, out_26);
  and and_30 (and_30_out, or_23_out, out_19);
  or or_24 (a2, and_24_out, and_25_out, and_26_out, and_27_out);
  or or_25 (a1, and_28_out, and_23_out);
  or or_26 (a0, and_29_out, and_30_out);
  Counter #(.width(3), .max('h7)) counter_1 (.Q(counter_1_q), .clk(CLK), .clr(SC_CLR));  // open: load, D, count, carry
  Decoder #(.select(3)) decoder_1 (
    .out0(out_2), .out1(out_5), .out2(out_9), .out3(out_12), .out4(out_15), .out5(out_19), .out6(out_22),
    .sel(counter_1_q));  // open: out7, en
  not not_15 (not_15_out, out_29[15]);
  Demultiplexer #(.select(3)) demultiplexer_1 (
    .out0(out_3), .out1(out_6), .out2(out_10), .out3(out_13), .out4(out_16), .out5(out_20), .out6(out_23),
    .out7(out_26), .in(1'b1), .sel(out_29[14:12]));  // open: en
  Clock clock_1 (.out(CLK));
  and and_31 (and_31_out, out_26, not_15_out, out_15);
  or or_27 (or_27_out, out_3, out_6, out_10);
  and and_32 (and_32_out, out_19, out_16);
  and and_33 (and_33_out, out_22, or_27_out);
  or or_28 (SC_CLR, and_31_out, and_33_out, and_32_out);

  assign {out_29[11], out_29[9], out_29[7:2]} = {out_27, out_24, out_21, out_17, out_14, out_11, out_7, out_4};

  // Other names for the same wires on the sheet: AC_OUT[15:0] = out_28; AC_15 = out_28[15]; AR_OUT[11:0] = out_8;
  //   D0 = out_3; D1 = out_6; D2 = out_10; D3 = out_13; D4 = out_16; D5 = out_20; D6 = out_23; D7 = out_26;
  //   DR_OUT[15:0] = out_25;
  //   ADD_FLD[11:0] = {out_27, out_29[10], out_24, out_29[8], out_21, out_17, out_14, out_11, out_7, out_4, out_29[1:0]};
  //   IR_OUT[15:0] = {out_29[15:12], out_27, out_29[10], out_24, out_29[8], out_21, out_17, out_14, out_11, out_7, out_4, out_29[1:0]};
  //   B2 = out_4; B3 = out_7; B4 = out_11; B5 = out_14; B6 = out_17; B7 = out_21; B9 = out_24; B11 = out_27;
  //   OPCODE[2:0] = out_29[14:12]; I_BIT = out_29[15]; MEM_OUT[15:0] = out_1; PC_OUT[11:0] = out_18; T0 = out_2;
  //   T1 = out_5; T2 = out_9; T3 = out_12; T4 = out_15; T5 = out_19; T6 = out_22

  // Notes on the sheet:
  //   MEMORY UNIT (RAM)
  //   ALU OPERATION
  //   BUS SYSTEM
  //   BUS SELECTION
  //   ARITHMATIC LOGICAL UNIT
  //   ALU SELECTION
  //   SEQUENCE COUNTER
  //   OPCODE DECODING
  //   OUTPUT WINDOW
endmodule

module seq_counter (
);

  wire and_1_out, and_2_out, and_3_out, CLK, D0, D1, D2, D4, D7, I_BIT, not_1_out, or_1_out, SC_CLR, T0, T1,
       T2, T3, T4, T5, T6;
  wire [2:0] counter_1_q;

  Counter #(.width(3), .max('h7)) counter_1 (.Q(counter_1_q), .clk(CLK), .clr(SC_CLR));  // open: load, D, count, carry
  Clock clock_1 (.out(CLK));
  Decoder #(.select(3)) decoder_1 (
    .out0(T0), .out1(T1), .out2(T2), .out3(T3), .out4(T4), .out5(T5), .out6(T6), .sel(counter_1_q));  // open: out7, en
  not not_1 (not_1_out, I_BIT);
  and and_1 (and_1_out, D7, not_1_out, T4);
  and and_2 (and_2_out, T6, or_1_out);
  or or_1 (or_1_out, D0, D1, D2);
  and and_3 (and_3_out, T5, D4);
  or or_2 (SC_CLR, and_1_out, and_2_out, and_3_out);
endmodule

module instr_decoder (
);

  wire D0, D1, D2, D3, D4, D5, D6, D7;
  wire [14:12] IR_OUT;

  Demultiplexer #(.select(3)) demultiplexer_1 (
    .out0(D0), .out1(D1), .out2(D2), .out3(D3), .out4(D4), .out5(D5), .out6(D6), .out7(D7), .in(1'b1),
    .sel(IR_OUT));  // open: en

  // Other names for the same wires on the sheet: OPCODE[2:0] = IR_OUT
endmodule

module ALU (
);

  wire a0, a1, a2, and_2_out, and_3_out, and_4_out, and_5_out, and_6_out, and_7_out, and_8_out, and_9_out,
       and_10_out, and_11_out, and_12_out, and_13_out, and_14_out, and_15_out, and_16_out, B5, B6, B7, B9,
       D0, D1, D2, D7, I_BIT, not_2_out, not_3_out, not_4_out, not_5_out, not_6_out, not_7_out, or_4_out,
       or_5_out, or_6_out, T3, T5, undriven;
  wire [15:0] AC_OUT, ALU_OUT, CIL, CIR, CMA_AC, DR_OUT, INC_AC, M_ADD, M_AND;

  assign CMA_AC = ~AC_OUT;  // NOT_Gate not_1, 16 bits wide
  Adder #(.width(16)) adder_1 (.a(AC_OUT), .b(16'h1), .out(INC_AC));  // open: cin, cout
  Adder #(.width(16)) adder_2 (.a(AC_OUT), .b(DR_OUT), .out(M_ADD));  // open: cin, cout
  Shifter #(.width(16), .shift("rr")) shifter_1 (.in(AC_OUT), .\dist (4'b0001), .out(CIR));
  Shifter #(.width(16), .shift("rl")) shifter_2 (.in(AC_OUT), .\dist (4'b0001), .out(CIL));
  assign M_AND = AC_OUT;  // AND_Gate and_1, 16 bits wide AND_Gate
  not not_2 (not_2_out, I_BIT);
  not not_3 (not_3_out, I_BIT);
  and and_2 (and_2_out, D0, T5);
  and and_3 (and_3_out, D2, T5);
  and and_4 (and_4_out, T3, not_2_out, B5, D7);
  and and_5 (and_5_out, D1, T5);
  and and_6 (and_6_out, T3, not_3_out, B9, D7);
  and and_7 (and_7_out, D1, T5);
  and and_8 (and_8_out, D2, T5);
  Multiplexer #(.select(3), .width(16)) multiplexer_1 (
    .in1(CMA_AC), .in2(INC_AC), .in3(M_ADD), .in4(M_AND), .in5(DR_OUT), .in6(CIR), .in7(CIL), .out(ALU_OUT),
    .sel({a2, a1, a0}));  // open: in0, en
  or or_1 (a2, and_2_out, and_3_out);
  or or_2 (a1, and_4_out, and_5_out);
  or or_3 (a0, and_6_out, and_7_out, and_8_out);
  not not_4 (not_4_out, I_BIT);
  not not_5 (not_5_out, I_BIT);
  or or_4 (or_4_out, B5, B7, B6);
  not not_6 (not_6_out, I_BIT);
  or or_5 (or_5_out, B9, B6);
  and and_9 (and_9_out, D0, T5);
  and and_10 (and_10_out, T3, not_4_out, B7, D7);
  and and_11 (and_11_out, T3, not_5_out, B6, D7);
  and and_12 (and_12_out, D2, T5);
  not not_7 (not_7_out, I_BIT);
  and and_13 (and_13_out, T3, not_7_out, D7, or_4_out);
  and and_14 (and_14_out, D1, T5);
  and and_15 (and_15_out, T3, not_6_out, or_5_out, D7);
  or or_6 (or_6_out, D1, D2);
  and and_16 (and_16_out, or_6_out, T5);
  or or_7 (a2, and_9_out, and_10_out, and_11_out, and_12_out);
  or or_8 (a1, and_13_out, and_14_out);
  or or_9 (a0, and_15_out, and_16_out, undriven);
endmodule

module MEMORY (
);

  wire and_1_out, and_2_out, CLK, D0, D1, D2, D7, I_BIT, not_1_out, or_1_out, or_2_out, T1, T3, T4;
  wire [11:0] BUS_OUT;
  wire [15:0] MEM_OUT;

  not not_1 (not_1_out, D7);
  or or_1 (or_1_out, D0, D1, D2);
  and and_1 (and_1_out, not_1_out, I_BIT, T3);
  and and_2 (and_2_out, T4, or_1_out);
  or or_2 (or_2_out, T1, and_1_out, and_2_out);
  RAM #(.addrWidth(12), .dataWidth(16)) ram_1 (
    .addr(BUS_OUT), .data(MEM_OUT), .sel(or_2_out), .clk(CLK), .ld(or_2_out));  // open: clr
endmodule

module AR_REG (
);

  wire and_1_out, CLK, D7, I_BIT, not_1_out, or_1_out, T0, T2, T3;
  wire [11:0] AR_OUT, BUS_OUT;

  and and_1 (and_1_out, T3, not_1_out, I_BIT);
  not not_1 (not_1_out, D7);
  or or_1 (or_1_out, T0, T2, and_1_out);
  Register #(.width(12)) register_1 (.D(BUS_OUT), .en(or_1_out), .Q(AR_OUT), .clk(CLK));  // open: clr
endmodule

module PC_REG (
);

  wire and_1_out, and_2_out, and_3_out, B3, B4, CLK, D4, D7, I_BIT, not_1_out, not_2_out, or_1_out, or_3_out,
       or_4_out, PC_INC, T1, T3, T4;
  wire [11:0] adder_1_out, BUS_OUT, multiplexer_1_out, PC_OUT;

  or or_1 (or_1_out, B3, B4);
  not not_1 (not_1_out, I_BIT);
  Adder #(.width(12)) adder_1 (.a(PC_OUT), .b(12'h1), .out(adder_1_out));  // open: cin, cout
  and and_1 (and_1_out, T3, or_1_out, D7, not_1_out);
  Multiplexer #(.width(12)) multiplexer_1 (
    .in0(BUS_OUT), .in1(adder_1_out), .out(multiplexer_1_out), .sel(PC_INC));  // open: en
  or or_2 (PC_INC, T1, and_1_out);
  or or_3 (or_3_out, B3, B4);
  not not_2 (not_2_out, I_BIT);
  and and_2 (and_2_out, T3, or_3_out, D7, not_2_out);
  and and_3 (and_3_out, T4, D4);
  Register #(.width(12)) register_1 (.D(multiplexer_1_out), .en(or_4_out), .Q(PC_OUT), .clk(CLK));  // open: clr
  or or_4 (or_4_out, T1, and_2_out, and_3_out);
endmodule

module DR_REG (
);

  wire and_1_out, CLK, D0, D1, D2, or_1_out, T4;
  wire [15:0] BUS_OUT, DR_OUT;

  or or_1 (or_1_out, D0, D1, D2);
  and and_1 (and_1_out, T4, or_1_out);
  Register #(.width(16)) register_1 (.D(BUS_OUT), .en(and_1_out), .Q(DR_OUT), .clk(CLK));  // open: clr
endmodule

module AC_REG (
);

  wire and_1_out, and_2_out, B5, B9, B11, CLK, D0, D1, D2, D7, I_BIT, not_1_out, not_2_out, or_1_out,
       or_2_out, or_3_out, or_4_out, T3, T5;
  wire [15:0] AC_OUT, ALU_OUT;

  not not_1 (not_1_out, I_BIT);
  or or_1 (or_1_out, B9, B5);
  or or_2 (or_2_out, D0, D1, D2);
  and and_1 (and_1_out, T3, not_1_out, or_1_out, D7);
  and and_2 (and_2_out, or_2_out, T5);
  Register #(.width(16)) register_1 (.D(ALU_OUT), .en(or_3_out), .Q(AC_OUT), .clk(CLK), .clr(or_4_out));
  or or_3 (or_3_out, and_1_out, and_2_out);
  or or_4 (or_4_out, not_2_out, D7, B11, T3);
  not not_2 (not_2_out, I_BIT);
endmodule

module IR_REG (
);

  wire CLK, T1;
  wire [15:0] BUS_OUT, IR_OUT;

  Register #(.width(16)) register_1 (.D(BUS_OUT), .en(T1), .Q(IR_OUT), .clk(CLK));  // open: clr
endmodule

module BUS (
);

  wire and_1_out, and_2_out, and_3_out, and_8_out, and_9_out, and_10_out, and_11_out, and_12_out, and_13_out,
       and_14_out, D0, D1, D2, D4, D7, I_BIT, not_1_out, not_2_out, not_3_out, not_4_out, or_1_out, or_2_out,
       or_3_out, or_4_out, or_5_out, or_6_out, or_7_out, or_8_out, s0, s1, s2, T0, T1, T2, T3, T4;
  wire [15:0] and_4_out, and_5_out, and_6_out, and_7_out, AR_OUT, BUS_OUT, IR_OUT, MEM_OUT,
       multiplexer_1_out, multiplexer_2_out, multiplexer_3_out, multiplexer_4_out, PC_OUT;

  not not_1 (not_1_out, D7);
  and and_1 (and_1_out, not_1_out, T3, I_BIT);
  or or_1 (or_1_out, D0, D1, D2);
  and and_2 (and_2_out, T4, or_1_out);
  or or_2 (or_2_out, T1, and_1_out, and_2_out);
  and and_3 (and_3_out, D4, T4);
  Multiplexer #(.width(16)) multiplexer_1 (
    .in0({16{1'b0}}), .in1({16{1'b1}}), .out(multiplexer_1_out), .sel(or_2_out));  // open: en
  Multiplexer #(.width(16)) multiplexer_2 (
    .in0({16{1'b0}}), .in1({16{1'b1}}), .out(multiplexer_2_out), .sel(and_3_out));  // open: en
  Multiplexer #(.width(16)) multiplexer_3 (
    .in0({16{1'b0}}), .in1({16{1'b1}}), .out(multiplexer_3_out), .sel(T0));  // open: en
  Multiplexer #(.width(16)) multiplexer_4 (
    .in0({16{1'b0}}), .in1({16{1'b1}}), .out(multiplexer_4_out), .sel(T2));  // open: en
  assign and_4_out = MEM_OUT & multiplexer_1_out;  // AND_Gate and_4, 16 bits wide
  assign and_5_out = AR_OUT & multiplexer_2_out;  // AND_Gate and_5, 16 bits wide
  assign and_6_out = PC_OUT & multiplexer_3_out;  // AND_Gate and_6, 16 bits wide
  assign and_7_out = IR_OUT & multiplexer_4_out;  // AND_Gate and_7, 16 bits wide
  not not_2 (not_2_out, D7);
  or or_3 (or_3_out, D0, D1, D2);
  not not_3 (not_3_out, D7);
  or or_4 (or_4_out, D0, D1, D2);
  not not_4 (not_4_out, D7);
  or or_5 (or_5_out, D0, D1, D2);
  and and_8 (and_8_out, not_2_out, T3, I_BIT);
  and and_9 (and_9_out, T4, or_3_out);
  and and_10 (and_10_out, not_3_out, T3, I_BIT);
  and and_11 (and_11_out, T4, or_4_out);
  and and_12 (and_12_out, not_4_out, T3, I_BIT);
  and and_13 (and_13_out, T4, or_5_out);
  Multiplexer #(.select(3), .width(16)) multiplexer_5 (
    .in1(AR_OUT), .in2(PC_OUT), .in5(IR_OUT), .in7(MEM_OUT), .out(BUS_OUT), .sel({s2, s1, s0}));  // open: in0, in3, in4, in6, en
  or or_6 (or_6_out, T1, and_8_out, and_9_out);
  or or_7 (or_7_out, T1, and_10_out, and_11_out);
  or or_8 (or_8_out, T1, and_12_out, and_13_out);
  and and_14 (and_14_out, D4, T4);
  or or_9 (s2, or_6_out, T2);
  or or_10 (s1, or_7_out, T0);
  or or_11 (s0, or_8_out, T2, and_14_out);
endmodule

module OUTPUT (
  output [15:0] out_1,
  output [15:0] out_2,
  output [15:0] out_3,
  output [15:0] out_4,
  output [15:0] out_5,
  output [15:0] out_6
);


  // Other names for the same wires on the sheet: AC_OUT[15:0] = out_5; AR_OUT[15:0] = out_2; DR_OUT[15:0] = out_4;
  //   IR_OUT[15:0] = out_6; MEM_OUT[15:0] = out_1; PC_OUT[15:0] = out_3
endmodule

module main (
  input  [15:0] in_1
);

  wire and_1_out, and_2_out, and_3_out, and_4_out, and_5_out, and_6_out, and_7_out, and_8_out, CLK, D0, D1,
       D2, D3, D4, D5, D6, D7, not_1_out, not_2_out, not_3_out, not_4_out, or_1_out, or_2_out, or_3_out,
       or_6_out, PC_INC, SC_CLR, T0, T1, T2, T3, T4, T5, T6;
  wire [2:0] counter_1_q;
  wire [11:0] adder_1_out, BUS_OUT, multiplexer_1_out, PC_OUT;
  wire [15:0] MEM_OUT;

  not not_1 (not_1_out, D7);
  or or_1 (or_1_out, D0, D1, D2);
  and and_1 (and_1_out, not_1_out, in_1[15], T3);
  and and_2 (and_2_out, T4, or_1_out);
  Demultiplexer #(.select(3)) demultiplexer_1 (
    .out0(D0), .out1(D1), .out2(D2), .out3(D3), .out4(D4), .out5(D5), .out6(D6), .out7(D7), .in(1'b1),
    .sel(in_1[14:12]));  // open: en
  or or_2 (or_2_out, T1, and_1_out, and_2_out);
  Decoder #(.select(3)) decoder_1 (
    .out0(T0), .out1(T1), .out2(T2), .out3(T3), .out4(T4), .out5(T5), .out6(T6), .sel(counter_1_q));  // open: out7, en
  Counter #(.width(3), .max('h7)) counter_1 (.Q(counter_1_q), .clk(CLK), .clr(SC_CLR));  // open: load, D, count, carry
  Clock clock_1 (.out(CLK));
  RAM #(.addrWidth(12), .dataWidth(16)) ram_1 (
    .addr(BUS_OUT), .data(MEM_OUT), .sel(or_2_out), .clk(CLK), .ld(or_2_out));  // open: clr
  not not_2 (not_2_out, in_1[15]);
  not not_3 (not_3_out, in_1[15]);
  and and_3 (and_3_out, D7, not_2_out, T4);
  and and_4 (and_4_out, T6, or_3_out);
  or or_3 (or_3_out, D0, D1, D2);
  and and_5 (and_5_out, T5, D4);
  and and_6 (and_6_out, T3, D7, not_3_out);
  Adder #(.width(12)) adder_1 (.a(PC_OUT), .b(12'h1), .out(adder_1_out));  // open: cin, cout
  or or_4 (PC_INC, T1, and_6_out);
  or or_5 (SC_CLR, and_3_out, and_4_out, and_5_out);
  Multiplexer #(.width(12)) multiplexer_1 (
    .in0(BUS_OUT), .in1(adder_1_out), .out(multiplexer_1_out), .sel(PC_INC));  // open: en
  not not_4 (not_4_out, in_1[15]);
  and and_7 (and_7_out, T3, D7, not_4_out);
  and and_8 (and_8_out, T4, D4);
  or or_6 (or_6_out, T1, and_7_out, and_8_out);
  Register #(.width(12)) register_1 (.D(multiplexer_1_out), .en(or_6_out), .Q(PC_OUT), .clk(CLK));  // open: clr

  // Other names for the same wires on the sheet: ADD_FLD[11:0] = in_1[11:0]; IR_OUT[15:0] = in_1;
  //   OPCODE[2:0] = in_1[14:12]; I_BIT = in_1[15]
endmodule
